# Fritzing sketch Ex_0_0_WiringAnLED (saved by Fritzing 0.9.2b)
breadboards: 1

parts:
  LED1 = smd LED [color="Red (633nm)" package="0805 [SMD]"]
  Part1 = Arduino Due (Rev2b)
  R1 = Resistor [tolerance=±5% resistance=220 package="2010 [SMD]"]

nets:
  N1: LED1.cathode, Part1.IOREF
  N2: LED1.anode, R1.Pin_0
  N3: Part1.GND, R1.Pin_1
