# Fritzing sketch Ex_2_0_SerialDebug_SingleLED (saved by Fritzing 0.9.2b)
breadboards: 1

parts:
  Part1 = Arduino Due (Rev2b)
  LED3 = smd LED [color="Green (555nm)" package="0805 [SMD]"]
  R1 = Resistor [tolerance=±5% resistance=220 package="0805 [SMD]"]

nets:
  N1: Part1.GND, R1.Pin_1
  N2: Part1.D10_PWM/SS0, LED3.cathode
  N3: LED3.anode, R1.Pin_0
