# Fritzing sketch Ex_3_0_ReadingAndWriting (saved by Fritzing 0.9.2b)
breadboards: 1

parts:
  Part1 = Arduino Due (Rev2b)
  LED1 = smd LED [color="Red (633nm)" package="0805 [SMD]"]
  LED2 = smd LED [color="Yellow (595nm)" package="1206 [SMD]"]
  LED3 = smd LED [color="Green (555nm)" package="0805 [SMD]"]
  R1 = Resistor [tolerance=±5% resistance=220 package="0805 [SMD]"]
  R2 = Resistor [tolerance=±5% resistance=220 package="0805 [SMD]"]
  R3 = Resistor [tolerance=±5% resistance=220 package="0805 [SMD]"]
  R4 = TRIMPOT [package=3386u]  # not connected

nets:
  N1: Part1.GND, R1.Pin_1, R2.Pin_1, R3.Pin_1
  N2: Part1.D10_PWM/SS0, LED3.cathode
  N3: Part1.D11_PWM, LED2.cathode
  N4: Part1.D12_PWM, LED1.cathode
  N5: LED1.anode, R3.Pin_0
  N6: LED2.anode, R2.Pin_0
  N7: LED3.anode, R1.Pin_0
