# Fritzing sketch Ex_3_1_ReadingAndWriting (saved by Fritzing 0.9.2b)

parts:
  Part1 = Arduino Due (Rev2b)
  R4 = TRIMPOT [package=3386u]

nets:
  N1: Part1.A0, R4.WIPER
  N2: Part1.IOREF, R4.CW
  N3: Part1.GND, R4.CCW
