# Fritzing sketch Ex_3_2_ReadingAndWriting (saved by Fritzing 0.9.2b)
breadboards: 1

parts:
  Part1 = Arduino Due (Rev2b)
  R4 = TRIMPOT [package=3386u]
  R5 = Resistor [tolerance=±5% resistance=220 package="0805 [SMD]"]
  LED1 = smd LED [color="Red (633nm)" package="0805 [SMD]"]

nets:
  N1: Part1.A0, R4.WIPER
  N2: Part1.IOREF, R4.CW
  N3: Part1.GND, R4.CCW, LED1.anode
  N4: Part1.D2_PWM, R5.Pin_1
  N5: R5.Pin_0, LED1.cathode
