# Fritzing sketch Ex_4_0_SensingAndActuation (saved by Fritzing 0.9.2b)
breadboards: 1

parts:
  Part1 = Arduino Due (Rev2b)
  JP1 = Header 6 [package=molex-1x6-ra_lock]
  U1 = L298_BRIDGE_DRIVER [package=powerso20]  # not connected
  M1 = DC Motor

nets:
  N1: Part1.IOREF, JP1.2
  N2: Part1.GND, JP1.5
  N3: Part1.D28, JP1.3, M1.pin_1
  N4: Part1.D29, JP1.4, M1.pin_2
